# Fritzing sketch LXF200 Advanced Tutorial (saved by Fritzing 0.9.1b)
breadboards: 1

parts:
  R1 = Resistor [tolerance=±5% resistance=220 package="0805 [SMD]"]
  LED1 = LED - 5mm [color="Red (633nm)" package="5 mm [THT]"]
  R2 = Resistor [tolerance=±5% resistance=220 package="0805 [SMD]"]
  LED2 = LED - 5mm [color="Red (633nm)" package="5 mm [THT]"]
  R3 = Resistor [tolerance=±5% resistance=220 package="0805 [SMD]"]
  LED3 = LED - 5mm [color="Red (633nm)" package="5 mm [THT]"]
  J1 = Piezo Speaker
  R4 = Resistor [tolerance=±5% resistance=220 package="0805 [SMD]"]
  Raspberry_Pi1 = Raspberry Pi B+
  S1 = Momentary Switch [package=ksa_sealed_tac_switch]

nets:
  N1: R1.Pin_0, Raspberry_Pi1.GPIO14
  N2: R1.Pin_1, LED1.anode
  N3: LED1.cathode, LED2.cathode, LED3.cathode, J1.pin1, Raspberry_Pi1.GND, S1.1
  N4: R2.Pin_0, Raspberry_Pi1.GPIO15
  N5: R2.Pin_1, LED2.anode
  N6: R3.Pin_0, Raspberry_Pi1.GPIO18
  N7: R3.Pin_1, LED3.anode
  N8: J1.pin2, R4.Pin_1
  N9: R4.Pin_0, Raspberry_Pi1.GPIO24
  N10: Raspberry_Pi1.GPIO21, S1.3

notes:
  This is the wire that we must not touch
  This is the wand with which we will navigate the wire. It is a series of 2 x male to female wires and 1 x female to female wire linked together with a paperclip hook attached.
